// Logisim project ASSINGMENT01.circ as structural Verilog: 4 circuits, main circuit main
module main (
  input  in_1,
  input  in_2,
  input  in_3,
  input  in_4
);

  wire n4_gate_and_gate_1_out_17, n4_gate_and_gate_2_out_17, n4_gate_and_gate_3_out_18,
       n4_gate_and_gate_4_out_17, n4_gate_and_gate_5_out_17, n4_gate_and_gate_6_out_17, n4_or_gate_1_out_17,
       NOT_2_out_6, NOT_3_out_6, not_gate_1_out_7, NOT_out_5;

  not_gate not_gate_1 (.in_1(in_1), .out_7(not_gate_1_out_7));  // open: in_2, in_3, in_4, out_5, out_6, out_8
  not_gate NOT (.in_1(in_2), .out_5(NOT_out_5), .out_6(NOT_out_5));  // open: in_2, in_3, in_4, out_7, out_8
  not_gate NOT_2 (.in_1(in_3), .out_6(NOT_2_out_6), .out_7(NOT_2_out_6));  // open: in_2, in_3, in_4, out_5, out_8
  not_gate NOT_3 (.in_1(in_4), .out_6(NOT_3_out_6));  // open: in_2, in_3, in_4, out_5, out_7, out_8
  _4_gate_AND_gate u_4_gate_and_gate_1 (
    .in_2(in_1), .in_3(NOT_out_5), .in_4(NOT_2_out_6), .in_5(in_4), .out_17(n4_gate_and_gate_1_out_17));  // open: in_1, in_6, in_7, in_8, in_9, in_10, in_11, in_12, in_13, in_14, in_15, in_16, out_18, out_19, out_20
  _4_gate_AND_gate u_4_gate_and_gate_2 (
    .in_2(in_1), .in_3(NOT_out_5), .in_4(in_3), .in_5(NOT_3_out_6), .out_17(n4_gate_and_gate_2_out_17));  // open: in_1, in_6, in_7, in_8, in_9, in_10, in_11, in_12, in_13, in_14, in_15, in_16, out_18, out_19, out_20
  _4_gate_AND_gate u_4_gate_and_gate_3 (
    .in_2(in_1), .in_3(NOT_out_5), .in_4(in_3), .in_5(in_4), .out_18(n4_gate_and_gate_3_out_18));  // open: in_1, in_6, in_7, in_8, in_9, in_10, in_11, in_12, in_13, in_14, in_15, in_16, out_17, out_19, out_20
  _4_gate_AND_gate u_4_gate_and_gate_4 (
    .in_2(in_1), .in_3(in_2), .in_4(NOT_2_out_6), .in_5(NOT_3_out_6), .out_17(n4_gate_and_gate_4_out_17));  // open: in_1, in_6, in_7, in_8, in_9, in_10, in_11, in_12, in_13, in_14, in_15, in_16, out_18, out_19, out_20
  _4_gate_AND_gate u_4_gate_and_gate_5 (
    .in_2(in_1), .in_3(in_2), .in_4(NOT_2_out_6), .in_5(in_4), .out_17(n4_gate_and_gate_5_out_17));  // open: in_1, in_6, in_7, in_8, in_9, in_10, in_11, in_12, in_13, in_14, in_15, in_16, out_18, out_19, out_20
  _4_gate_AND_gate u_4_gate_and_gate_6 (
    .in_2(in_1), .in_3(in_2), .in_4(in_3), .in_5(NOT_3_out_6), .out_17(n4_gate_and_gate_6_out_17));  // open: in_1, in_6, in_7, in_8, in_9, in_10, in_11, in_12, in_13, in_14, in_15, in_16, out_18, out_19, out_20
  _4_Gate_OR_gate u_4_or_gate_1 (
    .in_3(n4_gate_and_gate_1_out_17), .in_5(n4_gate_and_gate_2_out_17), .in_7(n4_gate_and_gate_3_out_18),
    .in_9(n4_gate_and_gate_4_out_17), .in_11(n4_gate_and_gate_5_out_17), .in_13(n4_gate_and_gate_6_out_17),
    .out_17(n4_or_gate_1_out_17));  // open: in_1, in_2, in_4, in_6, in_8, in_10, in_12, in_14, in_15, in_16, out_18, out_19, out_20

  // Notes on the sheet:
  //   A
  //   B
  //   C
  //   D
  //   AND
  //   AND
  //   AND
  //   AND
  //   AND
  //   AND
  //   OR
  //   F
endmodule

module _4_gate_AND_gate (
  input  in_1,
  input  in_2,
  input  in_3,
  input  in_4,
  input  in_5,
  input  in_6,
  input  in_7,
  input  in_8,
  input  in_9,
  input  in_10,
  input  in_11,
  input  in_12,
  input  in_13,
  input  in_14,
  input  in_15,
  input  in_16,
  output out_17,
  output out_18,
  output out_19,
  output out_20
);

  and and_1 (out_17, in_2, in_4, in_5, in_7);
  and and_2 (out_20, in_10, in_12, in_14, in_16);
  and and_3 (out_18, in_1, in_3, in_6, in_8);
  and and_4 (out_19, in_9, in_11, in_13, in_15);
endmodule

module _4_Gate_OR_gate (
  input  in_1,
  input  in_2,
  input  in_3,
  input  in_4,
  input  in_5,
  input  in_6,
  input  in_7,
  input  in_8,
  input  in_9,
  input  in_10,
  input  in_11,
  input  in_12,
  input  in_13,
  input  in_14,
  input  in_15,
  input  in_16,
  output out_17,
  output out_18,
  output out_19,
  output out_20
);

  or or_1 (out_17, in_1, in_3, in_5, in_7);
  or or_2 (out_20, in_10, in_12, in_14, in_16);
  or or_3 (out_19, in_9, in_11, in_13, in_15);
  or or_4 (out_18, in_2, in_4, in_6, in_8);
endmodule

module not_gate (
  input  in_1,
  input  in_2,
  input  in_3,
  input  in_4,
  output out_5,
  output out_6,
  output out_7,
  output out_8
);

  not not_1 (out_6, in_2);
  not not_2 (out_5, in_1);
  not not_3 (out_7, in_3);
  not not_4 (out_8, in_4);
endmodule
