// Logisim project lab 04.circ as structural Verilog: 4 circuits, main circuit main
module main (
  input  W,
  input  X,
  input  Y,
  input  Z,
  output A_W_XZ_XY,
  output B_X_prime_Z_X_prime_Y_XY_prime_Z_prime,
  output C_Y_prime_Z_prime_YZ,
  output D_Z_prime
);

  wire AND_2_out_13, AND_3_out_13, AND_4_out_13, AND_5_out_13, AND_out_13, n3_input_and_1_out_13,
       n3_input_and_2_out_13, not_gate_1_out_5, not_gate_2_out_5, not_gate_3_out_5;

  not_gate not_gate_1 (.in_1(W), .out_5(not_gate_1_out_5));  // open: in_2, in_3, in_4, out_6, out_7, out_8
  not_gate not_gate_2 (.in_1(X), .out_5(not_gate_2_out_5));  // open: in_2, in_3, in_4, out_6, out_7, out_8
  not_gate not_gate_3 (.in_1(Y), .out_5(not_gate_3_out_5));  // open: in_2, in_3, in_4, out_6, out_7, out_8
  not_gate not_gate_4 (.in_1(Z), .out_5(D_Z_prime));  // open: in_2, in_3, in_4, out_6, out_7, out_8
  _3_input_AND_Gate u_3_input_and_1 (
    .in_1(X), .in_3(Z), .out_13(n3_input_and_1_out_13));  // open: in_2, in_4, in_5, in_6, in_7, in_8, in_9, in_10, in_11, in_12, out_14, out_15, out_16
  _3_input_AND_Gate AND (
    .in_1(not_gate_2_out_5), .in_3(Z), .out_13(AND_out_13));  // open: in_2, in_4, in_5, in_6, in_7, in_8, in_9, in_10, in_11, in_12, out_14, out_15, out_16
  _3_input_AND_Gate u_3_input_and_2 (
    .in_2(X), .in_3(Y), .out_13(n3_input_and_2_out_13));  // open: in_1, in_4, in_5, in_6, in_7, in_8, in_9, in_10, in_11, in_12, out_14, out_15, out_16
  _3_input_AND_Gate AND_2 (
    .in_2(not_gate_2_out_5), .in_4(Y), .out_13(AND_2_out_13));  // open: in_1, in_3, in_5, in_6, in_7, in_8, in_9, in_10, in_11, in_12, out_14, out_15, out_16
  _3_input_AND_Gate AND_3 (
    .in_2(not_gate_3_out_5), .in_4(D_Z_prime), .out_13(AND_3_out_13));  // open: in_1, in_3, in_5, in_6, in_7, in_8, in_9, in_10, in_11, in_12, out_14, out_15, out_16
  _3_input_OR_gate u_3_input_or_gate_1 (
    .in_2(W), .in_3(n3_input_and_1_out_13), .in_5(n3_input_and_2_out_13), .out_13(A_W_XZ_XY));  // open: in_1, in_4, in_6, in_7, in_8, in_9, in_10, in_11, in_12, out_14, out_15, out_16
  _3_input_AND_Gate AND_4 (
    .in_1(X), .in_3(not_gate_3_out_5), .in_8(D_Z_prime), .out_13(AND_4_out_13));  // open: in_2, in_4, in_5, in_6, in_7, in_9, in_10, in_11, in_12, out_14, out_15, out_16
  _3_input_AND_Gate AND_5 (
    .in_1(Y), .in_3(Z), .out_13(AND_5_out_13));  // open: in_2, in_4, in_5, in_6, in_7, in_8, in_9, in_10, in_11, in_12, out_14, out_15, out_16
  _3_input_OR_gate OR (
    .in_1(AND_out_13), .in_3(AND_2_out_13), .in_5(AND_4_out_13),
    .out_13(B_X_prime_Z_X_prime_Y_XY_prime_Z_prime));  // open: in_2, in_4, in_6, in_7, in_8, in_9, in_10, in_11, in_12, out_14, out_15, out_16
  _3_input_OR_gate OR_2 (
    .in_1(AND_3_out_13), .in_4(AND_5_out_13), .out_13(C_Y_prime_Z_prime_YZ));  // open: in_2, in_3, in_5, in_6, in_7, in_8, in_9, in_10, in_11, in_12, out_14, out_15, out_16

  // Notes on the sheet:
  //   AND
  //   AND
  //   OR
endmodule

module _3_input_AND_Gate (
  input  in_1,
  input  in_2,
  input  in_3,
  input  in_4,
  input  in_5,
  input  in_6,
  input  in_7,
  input  in_8,
  input  in_9,
  input  in_10,
  input  in_11,
  input  in_12,
  output out_13,
  output out_14,
  output out_15,
  output out_16
);

  and and_1 (out_13, in_1, in_3, in_6);
  and and_2 (out_16, in_8, in_10, in_10, in_12);
  and and_3 (out_15, in_7, in_7, in_9, in_9, in_11);
  and and_4 (out_14, in_2, in_4, in_5);
endmodule

module _3_input_OR_gate (
  input  in_1,
  input  in_2,
  input  in_3,
  input  in_4,
  input  in_5,
  input  in_6,
  input  in_7,
  input  in_8,
  input  in_9,
  input  in_10,
  input  in_11,
  input  in_12,
  output out_13,
  output out_14,
  output out_15,
  output out_16
);

  or or_1 (out_14, in_2, in_4, in_6);
  or or_2 (out_16, in_8, in_10, in_12);
  or or_3 (out_13, in_1, in_3, in_5);
  or or_4 (out_15, in_7, in_9, in_11);
endmodule

module not_gate (
  input  in_1,
  input  in_2,
  input  in_3,
  input  in_4,
  output out_5,
  output out_6,
  output out_7,
  output out_8
);

  not not_1 (out_5, in_1);
  not not_2 (out_6, in_2);
  not not_3 (out_7, in_3);
  not not_4 (out_8, in_4);
endmodule
