// Logisim project lab05 exp2.circ as structural Verilog: 1 circuit, main circuit main
module main (
  input  C,
  input  C_2,
  input  A0,
  input  B0,
  input  A1,
  input  B1,
  input  A2,
  input  B2,
  input  A3,
  input  B3
);

  wire adder_1_cout, adder_2_cout, adder_3_cout, adder_4_cout, adder_5_cout, adder_6_cout, adder_7_cout,
       and_1_out, and_2_out, or_2_out;
  wire [3:0] adder_1_out, adder_2_out, adder_3_out, adder_4_out, adder_5_out, adder_6_out, adder_7_out,
       adder_8_out, or_1_out;
  wire [3:1] undriven, undriven_2, undriven_3, undriven_4, undriven_5, undriven_6, undriven_7, undriven_8,
       undriven_9;

  Adder #(.width(4)) adder_1 (
    .a({undriven, A0}), .b({undriven_2, B0}), .out(adder_1_out), .cin(C_2), .cout(adder_1_cout));
  Adder #(.width(4)) adder_2 (
    .a({undriven_3, A1}), .b({undriven_4, B1}), .out(adder_2_out), .cin(adder_1_cout), .cout(adder_2_cout));
  Adder #(.width(4)) adder_3 (
    .a({undriven_5, A2}), .b({undriven_6, B2}), .out(adder_3_out), .cin(adder_2_cout), .cout(adder_3_cout));
  Adder #(.width(4)) adder_4 (
    .a({undriven_7, A3}), .b({undriven_8, B3}), .out(adder_4_out), .cin(adder_3_cout), .cout(adder_4_cout));
  and and_1 (and_1_out, adder_4_out[0], adder_3_out[0]);
  or or_1 (or_1_out[0], adder_4_cout, or_2_out);
  or or_2 (or_2_out, and_1_out, and_2_out);
  and and_2 (and_2_out, adder_4_out[0], adder_2_out[0]);
  Adder #(.width(4)) adder_5 (.a({undriven_9, 1'b0}), .b(adder_1_out), .out(adder_5_out), .cin(C), .cout(adder_5_cout));
  Adder #(.width(4)) adder_6 (
    .a(or_1_out), .b(adder_2_out), .out(adder_6_out), .cin(adder_5_cout), .cout(adder_6_cout));
  Adder #(.width(4)) adder_7 (
    .a(or_1_out), .b(adder_3_out), .out(adder_7_out), .cin(adder_6_cout), .cout(adder_7_cout));
  Adder #(.width(4)) adder_8 (
    .a({undriven_9, 1'b0}), .b(adder_4_out), .out(adder_8_out), .cin(adder_7_cout));  // open: cout
  // Pins of 1 and 4 bits meet at {undriven, A0}
  // Pins of 1 and 4 bits meet at {undriven_2, B0}
  // Pins of 1 and 4 bits meet at {undriven_5, A2}
  // Pins of 1 and 4 bits meet at {undriven_6, B2}
  // Pins of 1 and 4 bits meet at adder_3_out
  // Pins of 1 and 4 bits meet at adder_4_out
  // Pins of 1 and 4 bits meet at adder_2_out
  // Pins of 1 and 4 bits meet at or_1_out
  // Pins of 1 and 4 bits meet at {undriven_3, A1}
  // Pins of 1 and 4 bits meet at {undriven_4, B1}
  // Pins of 1 and 4 bits meet at {undriven_9, 1'b0}
  // Pins of 1 and 4 bits meet at {undriven_8, B3}

  // Notes on the sheet:
  //   S0
  //   S1
  //   S2
  //   S3
endmodule
