// Logisim project lab5 exp1.circ as structural Verilog: 1 circuit, main circuit main
module main (
  input  [3:0] A,
  input  [3:0] B,
  input  M,
  output [3:0] Sum,
  output carry_out
);

  wire adder_1_cout, adder_2_cout, adder_3_cout, xor_1_out, xor_2_out, xor_3_out, xor_4_out;

  xor xor_1 (xor_1_out, B[0], M);
  xor xor_2 (xor_2_out, B[1], M);
  xor xor_3 (xor_3_out, B[2], M);
  xor xor_4 (xor_4_out, B[3], M);
  Adder #(.width(1)) adder_1 (.a(A[0]), .b(xor_1_out), .out(Sum[0]), .cin(M), .cout(adder_1_cout));
  Adder #(.width(1)) adder_2 (.a(A[1]), .b(xor_2_out), .out(Sum[1]), .cin(adder_1_cout), .cout(adder_2_cout));
  Adder #(.width(1)) adder_3 (.a(A[2]), .b(xor_3_out), .out(Sum[2]), .cin(adder_2_cout), .cout(adder_3_cout));
  Adder #(.width(1)) adder_4 (.a(A[3]), .b(xor_4_out), .out(Sum[3]), .cin(adder_3_cout), .cout(carry_out));
endmodule
