// Logisim project lab6.Q1.circ as structural Verilog: 1 circuit, main circuit main
module main (
  input  S1,
  input  S0,
  input  I0,
  input  I1,
  input  I2,
  input  I3,
  output OUTPUT
);

  wire multiplexer_1_out, multiplexer_2_out, not_1_out;
  wire [1:1] undriven;

  not not_1 (not_1_out, S0);
  Multiplexer #(.select(2)) multiplexer_1 (
    .in1(I0), .in3(I1), .out(multiplexer_1_out), .sel({undriven[1], S1}), .en(not_1_out));  // open: in0, in2
  Multiplexer #(.select(2)) multiplexer_2 (
    .in1(I2), .in3(I3), .out(multiplexer_2_out), .sel({undriven[1], S1}), .en(S0));  // open: in0, in2
  or or_1 (OUTPUT, multiplexer_1_out, multiplexer_2_out);
  // Pins of 1 and 2 bits meet at {undriven[1], S1}
endmodule
