// Logisim project max term.circ as structural Verilog: 5 circuits, main circuit main
module main (
  input  A,
  input  B,
  input  C
);

  wire AND_out_25, not_2_out_8, not_3_out_8, not_out_9, OR_2_out_13, OR_3_out_13, OR_4_out_13, OR_5_out_13,
       OR_out_13;

  NOT_gate \not  (
    .in_1(A), .out_9(not_out_9));  // open: in_2, in_3, in_4, in_5, in_6, out_7, out_8, out_10, out_11, out_12
  NOT_gate not_2 (
    .in_1(B), .out_8(not_2_out_8));  // open: in_2, in_3, in_4, in_5, in_6, out_7, out_9, out_10, out_11, out_12
  NOT_gate not_3 (
    .in_1(C), .out_8(not_3_out_8));  // open: in_2, in_3, in_4, in_5, in_6, out_7, out_9, out_10, out_11, out_12
  _3_input_OR_gate OR (
    .in_8(not_out_9), .in_9(not_2_out_8), .in_10(not_3_out_8), .out_13(OR_out_13));  // open: in_1, in_2, in_3, in_4, in_5, in_6, in_7, in_11, in_12, out_14, out_15, out_16
  _3_input_OR_gate OR_2 (
    .in_1(not_out_9), .in_2(B), .in_3(C), .out_13(OR_2_out_13));  // open: in_4, in_5, in_6, in_7, in_8, in_9, in_10, in_11, in_12, out_14, out_15, out_16
  _3_input_OR_gate OR_3 (
    .in_1(A), .in_2(A), .in_3(not_2_out_8), .in_4(not_3_out_8), .out_13(OR_3_out_13));  // open: in_5, in_6, in_7, in_8, in_9, in_10, in_11, in_12, out_14, out_15, out_16
  _3_input_OR_gate OR_4 (
    .in_1(not_2_out_8), .in_2(C), .in_3(A), .out_13(OR_4_out_13));  // open: in_4, in_5, in_6, in_7, in_8, in_9, in_10, in_11, in_12, out_14, out_15, out_16
  _3_input_OR_gate OR_5 (
    .in_1(A), .in_3(B), .in_6(C), .out_13(OR_5_out_13));  // open: in_2, in_4, in_5, in_7, in_8, in_9, in_10, in_11, in_12, out_14, out_15, out_16
  _5_input_AND_gate AND (
    .in_1(OR_out_13), .in_3(OR_2_out_13), .in_6(OR_3_out_13), .in_10(OR_4_out_13), .in_12(OR_5_out_13),
    .out_25(AND_out_25));  // open: in_2, in_4, in_5, in_7, in_8, in_9, in_11, in_13, in_14, in_15, in_16, in_17, in_18, in_19, in_20, in_21, in_22, in_23, in_24, out_26, out_27, out_28, out_29, out_30, out_31, out_32

  // Notes on the sheet:
  //   F2
  //   (A'+B'+C')(A'+B+C)(A+B'+C')(A+B'+C)(A+B+C)
endmodule

module _3_input_AND_gate (
  input  in_1,
  input  in_2,
  input  in_3,
  input  in_4,
  input  in_5,
  input  in_6,
  input  in_7,
  input  in_8,
  input  in_9,
  input  in_10,
  input  in_11,
  input  in_12,
  output out_13,
  output out_14,
  output out_15,
  output out_16
);

  and and_1 (out_13, in_1, in_2, in_3);
  and and_2 (out_14, in_4, in_5, in_6);
  and and_3 (out_15, in_7, in_8, in_9);
  and and_4 (out_16, in_10, in_11, in_11, in_11);
endmodule

module _3_input_OR_gate (
  input  in_1,
  input  in_2,
  input  in_3,
  input  in_4,
  input  in_5,
  input  in_6,
  input  in_7,
  input  in_8,
  input  in_9,
  input  in_10,
  input  in_11,
  input  in_12,
  output out_13,
  output out_14,
  output out_15,
  output out_16
);

  or or_1 (out_13, in_1, in_2, in_3);
  or or_2 (out_14, in_4, in_5, in_6);
  or or_3 (out_15, in_7, in_8, in_9);
  or or_4 (out_16, in_10, in_11, in_12);
endmodule

module NOT_gate (
  input  in_1,
  input  in_2,
  input  in_3,
  input  in_4,
  input  in_5,
  input  in_6,
  output out_7,
  output out_8,
  output out_9,
  output out_10,
  output out_11,
  output out_12
);

  not not_1 (out_7, in_1);
  not not_2 (out_8, in_2);
  not not_3 (out_9, in_3);
  not not_4 (out_10, in_4);
  not not_5 (out_11, in_5);
  not not_6 (out_12, in_6);
endmodule

module _5_input_AND_gate (
  input  in_1,
  input  in_2,
  input  in_3,
  input  in_4,
  input  in_5,
  input  in_6,
  input  in_7,
  input  in_8,
  input  in_9,
  input  in_10,
  input  in_11,
  input  in_12,
  input  in_13,
  input  in_14,
  input  in_15,
  input  in_16,
  input  in_17,
  input  in_18,
  input  in_19,
  input  in_20,
  input  in_21,
  input  in_22,
  input  in_23,
  input  in_24,
  output out_25,
  output out_26,
  output out_27,
  output out_28,
  output out_29,
  output out_30,
  output out_31,
  output out_32
);

  and and_1 (out_26, in_2, in_4, in_6);
  and and_2 (out_28, in_8, in_10, in_12);
  and and_3 (out_29, in_13, in_15, in_17);
  and and_4 (out_31, in_19, in_21, in_23);
  and and_5 (out_25, in_1, in_3, in_5);
  and and_6 (out_27, in_7, in_9, in_11);
  and and_7 (out_30, in_14, in_16, in_18);
  and and_8 (out_32, in_20, in_22, in_24);
endmodule
