// Logisim project min term.circ as structural Verilog: 4 circuits, main circuit main
module main (
  input  A,
  input  B,
  input  C
);

  wire AND_2_out_13, AND_3_out_13, AND_out_13, not_2_out_8, not_3_out_8, not_out_8, OR_out_13;

  not_gate \not  (
    .in_1(A), .out_8(not_out_8));  // open: in_2, in_3, in_4, in_5, in_6, out_7, out_9, out_10, out_11, out_12
  not_gate not_2 (
    .in_1(B), .out_8(not_2_out_8));  // open: in_2, in_3, in_4, in_5, in_6, out_7, out_9, out_10, out_11, out_12
  not_gate not_3 (
    .in_1(C), .out_8(not_3_out_8));  // open: in_2, in_3, in_4, in_5, in_6, out_7, out_9, out_10, out_11, out_12
  _3_input_AND_gate AND (
    .in_1(not_out_8), .in_3(B), .in_5(not_3_out_8), .out_13(AND_out_13));  // open: in_2, in_4, in_6, in_7, in_8, in_9, in_10, in_11, in_12, out_14, out_15, out_16
  _3_input_AND_gate AND_2 (
    .in_1(A), .in_3(B), .in_5(not_3_out_8), .out_13(AND_2_out_13));  // open: in_2, in_4, in_6, in_7, in_8, in_9, in_10, in_11, in_12, out_14, out_15, out_16
  _3_input_AND_gate AND_3 (
    .in_2(not_out_8), .in_3(not_2_out_8), .in_5(C), .out_13(AND_3_out_13));  // open: in_1, in_4, in_6, in_7, in_8, in_9, in_10, in_11, in_12, out_14, out_15, out_16
  _3_input_OR_gate OR (
    .in_2(AND_3_out_13), .in_4(AND_out_13), .in_5(AND_out_13), .in_7(AND_2_out_13), .out_13(OR_out_13));  // open: in_1, in_3, in_6, in_8, in_9, in_10, in_11, in_12, out_14, out_15, out_16

  // Notes on the sheet:
  //   F1
  //   A'B'C+A'BC'+ABC'
  //   min term
endmodule

module _3_input_AND_gate (
  input  in_1,
  input  in_2,
  input  in_3,
  input  in_4,
  input  in_5,
  input  in_6,
  input  in_7,
  input  in_8,
  input  in_9,
  input  in_10,
  input  in_11,
  input  in_12,
  output out_13,
  output out_14,
  output out_15,
  output out_16
);

  and and_1 (out_13, in_1, in_2, in_3);
  and and_2 (out_14, in_4, in_5, in_6);
  and and_3 (out_15, in_7, in_8, in_9);
  and and_4 (out_16, in_10, in_11, in_11, in_11);
endmodule

module _3_input_OR_gate (
  input  in_1,
  input  in_2,
  input  in_3,
  input  in_4,
  input  in_5,
  input  in_6,
  input  in_7,
  input  in_8,
  input  in_9,
  input  in_10,
  input  in_11,
  input  in_12,
  output out_13,
  output out_14,
  output out_15,
  output out_16
);

  or or_1 (out_13, in_1, in_2, in_3);
  or or_2 (out_14, in_4, in_5, in_6);
  or or_3 (out_15, in_7, in_8, in_9);
  or or_4 (out_16, in_10, in_11, in_12);
endmodule

module not_gate (
  input  in_1,
  input  in_2,
  input  in_3,
  input  in_4,
  input  in_5,
  input  in_6,
  output out_7,
  output out_8,
  output out_9,
  output out_10,
  output out_11,
  output out_12
);

  not not_1 (out_7, in_1);
  not not_2 (out_8, in_2);
  not not_3 (out_9, in_3);
  not not_4 (out_10, in_4);
  not not_5 (out_11, in_5);
  not not_6 (out_12, in_6);
endmodule
